// Logisim project BinaryAdder.circ as structural Verilog: 1 circuit, main circuit main
module main (
  input  in_1,
  input  in_2,
  input  in_3,
  input  in_4,
  input  in_5,
  input  in_6,
  input  in_7,
  input  in_8,
  input  in_9,
  input  in_10,
  input  in_11,
  input  in_12,
  input  in_13,
  input  in_14,
  input  in_15,
  input  in_16,
  input  in_17,
  input  in_18,
  input  in_19,
  input  in_20,
  output out_21,
  output out_22,
  output out_23,
  output out_24,
  output out_25,
  output out_26,
  output out_27,
  output out_28,
  output out_29,
  output out_30,
  output out_31
);

  wire and_1_out, and_2_out, and_3_out, and_4_out, and_5_out, and_6_out, and_7_out, and_8_out, and_9_out,
       xor_2_out, xor_3_out, xor_4_out, xor_5_out, xor_6_out, xor_7_out, xor_8_out, xor_9_out, xor_10_out;

  xor xor_1 (out_21, in_1, in_2);
  xor xor_2 (xor_2_out, in_3, in_4);
  xor xor_3 (xor_3_out, in_5, in_6);
  xor xor_4 (xor_4_out, in_7, in_8);
  xor xor_5 (xor_5_out, in_9, in_10);
  xor xor_6 (xor_6_out, in_11, in_12);
  xor xor_7 (xor_7_out, in_13, in_14);
  xor xor_8 (xor_8_out, in_15, in_16);
  xor xor_9 (xor_9_out, in_17, in_18);
  xor xor_10 (xor_10_out, in_19, in_20);
  and and_1 (and_1_out, in_1, in_2);
  and and_2 (and_2_out, in_3, in_4);
  and and_3 (and_3_out, in_5, in_6);
  and and_4 (and_4_out, in_7, in_8);
  and and_5 (and_5_out, in_9, in_10);
  and and_6 (and_6_out, in_11, in_12);
  and and_7 (and_7_out, in_13, in_14);
  and and_8 (and_8_out, in_15, in_16);
  and and_9 (and_9_out, in_17, in_18);
  and and_10 (out_31, in_19, in_20);
  xor xor_11 (out_22, and_1_out, xor_2_out);
  xor xor_12 (out_23, and_2_out, xor_3_out);
  xor xor_13 (out_24, and_3_out, xor_4_out);
  xor xor_14 (out_25, and_4_out, xor_5_out);
  xor xor_15 (out_26, and_5_out, xor_6_out);
  xor xor_16 (out_27, and_6_out, xor_7_out);
  xor xor_17 (out_28, and_7_out, xor_8_out);
  xor xor_18 (out_29, and_8_out, xor_9_out);
  xor xor_19 (out_30, and_9_out, xor_10_out);
endmodule
